// Logisim project control_logic.circ as structural Verilog: 12 circuits, main circuit control_logic
module control_logic (
  input  [31:0] inst,
  input  BrEq,
  input  BrLt,
  output out_4,
  output out_5,
  output [2:0] out_6,
  output out_7,
  output out_8,
  output out_9,
  output [3:0] out_10,
  output out_11,
  output [1:0] out_12,
  output out_13,
  output out_14
);

  wire [6:0] undriven;

  PCSel_processor pcsel_processor_1 (
    .Opcode(inst[6:0]), .Funct3(inst[14:12]), .BrEq(BrEq), .BrLt(BrLt), .PCSel_Out(out_4));
  RegWEn_processor regwen_processor_1 (.Opcode(inst[6:0]), .RegWEn_Out(out_5));
  ImmSel_processor immsel_processor_1 (.Opcode(inst[6:0]), .Funct3(inst[14:12]), .ImmSel_Out(out_6));
  BrUn_processor brun_processor_1 (.Opcode(inst[6:0]), .Funct3(inst[14:12]), .BrUn_Out(out_7));
  ASel_processor asel_processor_1 (.Opcode(inst[6:0]), .ASel_Out(out_8));
  BSel_processor bsel_processor_1 (.Opcode(inst[6:0]), .BSel_Out(out_9));
  BrSel_processor brsel_processor_1 (.Opcode(inst[6:0]), .Funct3(inst[14:12]), .BrSel_Out(out_13));
  AddrSel_processor addrsel_processor_1 (
    .Opcode(inst[6:0]), .Funct3(inst[14:12]), .BrEq(BrEq), .BrLt(BrLt), .AddrSel_Out(out_14));
  MemRW_processor memrw_processor_1 (
    .Opcode(inst[6:0]), .Funct3(inst[14:12]), .BrEq(BrEq), .BrLt(BrLt), .MemRW_Out(out_11));
  WBSel_processor wbsel_processor_1 (.Opcode(inst[6:0]), .Funct3(inst[14:12]), .WBSel_Out(out_12));
  ALUSel_processor alusel_processor_1 (
    .Opcode(inst[6:0]), .Funct3(inst[14:12]), .Funct7(undriven), .ALUSel_Out(out_10));

  // Other names for the same wires on the sheet: AddrSel = out_14; ALUSel[3:0] = out_10; ASel = out_8; BrSel = out_13;
  //   BrUn = out_7; BSel = out_9; ImmSel[2:0] = out_6; Opcode[6:0] = inst[6:0]; Funct3[2:0] = inst[14:12];
  //   Funct7[6:0] = inst[31:25]; MemRW = out_11; PCSel = out_4; RegWEn = out_5; WBSel[1:0] = out_12

  // Notes on the sheet:
  //   INPUTS to your circuit
  //   DON'T CHANGE THE LOCATIONS OF THE INPUTS AND OUTPUTS!
  //   OUTPUT from your circuit
endmodule

module PCSel_processor (
  input  [6:0] Opcode,
  input  [2:0] Funct3,
  input  BrEq,
  input  BrLt,
  output PCSel_Out
);

  wire Funct3_000, Funct3_001, Funct3_100, Funct3_101, Funct3_110, Funct3_111, Funct3_Result, or_1_out;

  Multiplexer #(.enable("false"), .select(2)) multiplexer_1 (
    .in0(1'b0), .in1(1'b0), .in2(1'b1), .out(Funct3_000), .sel({BrEq, BrLt}));  // open: in3
  Multiplexer #(.enable("false"), .select(2)) multiplexer_2 (
    .in0(1'b1), .in1(1'b1), .in2(1'b0), .out(Funct3_001), .sel({BrEq, BrLt}));  // open: in3
  Multiplexer #(.enable("false"), .select(2)) multiplexer_3 (
    .in0(1'b0), .in1(1'b1), .in2(1'b0), .out(Funct3_100), .sel({BrEq, BrLt}));  // open: in3
  Multiplexer #(.enable("false"), .select(2)) multiplexer_4 (
    .in0(1'b1), .in1(1'b0), .in2(1'b1), .out(Funct3_101), .sel({BrEq, BrLt}));  // open: in3
  or or_1 (or_1_out, Opcode[2], Funct3_Result);
  and and_1 (PCSel_Out, Opcode[6], or_1_out);
  Multiplexer #(.enable("false"), .select(2)) multiplexer_5 (
    .in0(1'b0), .in1(1'b1), .in2(1'b0), .out(Funct3_110), .sel({BrEq, BrLt}));  // open: in3
  Multiplexer #(.enable("false"), .select(2)) multiplexer_6 (
    .in0(1'b1), .in1(1'b0), .in2(1'b1), .out(Funct3_111), .sel({BrEq, BrLt}));  // open: in3
  Multiplexer #(.enable("false"), .select(3)) multiplexer_7 (
    .in0(Funct3_000), .in1(Funct3_001), .in4(Funct3_100), .in5(Funct3_101), .in6(Funct3_110),
    .in7(Funct3_111), .out(Funct3_Result), .sel(Funct3));  // open: in2, in3

  // Other names for the same wires on the sheet: Br[1:0] = {BrEq, BrLt}; PCSel = PCSel_Out

  // Notes on the sheet:
  //   INPUT
  //   OUTPUT
endmodule

module RegWEn_processor (
  input  [6:0] Opcode,
  output RegWEn_Out
);

  wire and_1_out;

  and and_1 (and_1_out, ~Opcode[2], ~Opcode[3], ~Opcode[4], Opcode[5]);  // AND_Gate
  not not_1 (RegWEn_Out, and_1_out);

  // Other names for the same wires on the sheet: RegWEn = RegWEn_Out

  // Notes on the sheet:
  //   INPUT
  //   OUTPUT
endmodule

module ImmSel_processor (
  input  [6:0] Opcode,
  input  [2:0] Funct3,
  output [2:0] ImmSel_Out
);

  wire and_5_out, and_10_out, I000, I_jalr, I_load, IR, IR101, not_1_out, not_2_out, not_3_out, not_4_out,
       not_5_out, not_6_out, not_7_out, not_8_out, not_9_out, not_10_out, not_11_out, not_12_out, not_13_out,
       not_14_out, not_15_out, not_16_out, not_17_out, not_18_out, not_19_out, not_20_out, not_21_out,
       not_22_out, not_23_out, S001, SB010, U011, UJ100;
  wire [2:0] bitfinder_1_index;

  not not_1 (not_1_out, Opcode[2]);
  not not_2 (not_2_out, Opcode[3]);
  not not_3 (not_3_out, Opcode[4]);
  not not_4 (not_4_out, Opcode[6]);
  not not_5 (not_5_out, Opcode[2]);
  not not_6 (not_6_out, Opcode[3]);
  not not_7 (not_7_out, Opcode[4]);
  not not_8 (not_8_out, Opcode[3]);
  not not_9 (not_9_out, Opcode[6]);
  and and_1 (S001, not_1_out, not_2_out, not_3_out, Opcode[5], not_4_out);
  and and_2 (SB010, not_5_out, not_6_out, not_7_out, Opcode[5], Opcode[6]);
  and and_3 (U011, Opcode[2], not_8_out, Opcode[4], not_9_out);
  not not_10 (not_10_out, Opcode[4]);
  not not_11 (not_11_out, Opcode[3]);
  not not_12 (not_12_out, Opcode[4]);
  not not_13 (not_13_out, Opcode[2]);
  not not_14 (not_14_out, Opcode[3]);
  not not_15 (not_15_out, Opcode[4]);
  not not_16 (not_16_out, Opcode[5]);
  not not_17 (not_17_out, Opcode[6]);
  not not_18 (not_18_out, Opcode[2]);
  not not_19 (not_19_out, Opcode[3]);
  not not_20 (not_20_out, Opcode[5]);
  not not_21 (not_21_out, Opcode[6]);
  not not_22 (not_22_out, Funct3[1]);
  and and_4 (IR, not_18_out, not_19_out, not_20_out, not_21_out);
  and and_5 (and_5_out, Funct3[0], not_22_out);
  BitFinder #(.width(6)) bitfinder_1 (
    .in({IR101, UJ100, U011, SB010, S001, I000}), .index(bitfinder_1_index));  // open: found
  and and_6 (IR101, IR, and_5_out);
  and and_7 (UJ100, Opcode[2], Opcode[3], not_10_out, Opcode[5], Opcode[6]);
  and and_8 (I_jalr, Opcode[2], not_11_out, not_12_out, Opcode[5], Opcode[6]);
  and and_9 (I_load, not_13_out, not_14_out, not_15_out, not_16_out, not_17_out);
  Multiplexer #(.enable("false"), .select(3), .width(3)) multiplexer_1 (
    .in0(3'b000), .in1(3'b001), .in2(3'b010), .in3(3'b011), .in4(3'b100), .in5(3'b101), .out(ImmSel_Out),
    .sel(bitfinder_1_index));  // open: in6, in7
  not not_23 (not_23_out, IR101);
  and and_10 (and_10_out, IR, not_23_out);
  or or_1 (I000, I_jalr, I_load, and_10_out);

  // Other names for the same wires on the sheet: ImmSel[2:0] = ImmSel_Out

  // Notes on the sheet:
  //   INPUT
  //   OUTPUT
endmodule

module BrUn_processor (
  input  [6:0] Opcode,
  input  [2:0] Funct3,
  output BrUn_Out
);

  and and_1 (BrUn_Out, ~Opcode[2], ~Opcode[3], ~Opcode[4], Opcode[5], Opcode[6], Funct3[1], Funct3[2]);  // AND_Gate

  // Other names for the same wires on the sheet: BrUn = BrUn_Out

  // Notes on the sheet:
  //   INPUT
  //   OUTPUT
endmodule

module ASel_processor (
  input  [6:0] Opcode,
  output ASel_Out
);

  wire SB, U, UJ;

  and and_1 (SB, ~Opcode[2], ~Opcode[3], ~Opcode[4], Opcode[5], Opcode[6]);  // AND_Gate
  and and_2 (U, Opcode[2], ~Opcode[3], Opcode[4], ~Opcode[6]);  // AND_Gate
  and and_3 (UJ, Opcode[2], Opcode[3], ~Opcode[4], Opcode[5], Opcode[6]);  // AND_Gate
  or or_1 (ASel_Out, SB, U, UJ);

  // Other names for the same wires on the sheet: ASel = ASel_Out

  // Notes on the sheet:
  //   INPUT
  //   OUTPUT
endmodule

module BSel_processor (
  input  [6:0] Opcode,
  output BSel_Out
);

  wire and_1_out;

  and and_1 (and_1_out, ~Opcode[2], ~Opcode[3], Opcode[4], Opcode[5], ~Opcode[6]);  // AND_Gate
  not not_1 (BSel_Out, and_1_out);

  // Other names for the same wires on the sheet: BSel = BSel_Out
endmodule

module BrSel_processor (
  input  [6:0] Opcode,
  input  [2:0] Funct3,
  output BrSel_Out
);

  and and_1 (BrSel_Out, ~Opcode[2], ~Opcode[3], ~Opcode[4], Opcode[5], ~Opcode[6]);  // AND_Gate

  // Other names for the same wires on the sheet: BrSel = BrSel_Out

  // Notes on the sheet:
  //   INPUT
  //   OUTPUT
endmodule

module AddrSel_processor (
  input  [6:0] Opcode,
  input  [2:0] Funct3,
  input  BrEq,
  input  BrLt,
  output AddrSel_Out
);

  and and_1 (AddrSel_Out, ~Opcode[2], ~Opcode[3], ~Opcode[4], Opcode[5], ~Opcode[6], Funct3[0], Funct3[0], Funct3[0], ~BrEq, BrLt);  // AND_Gate

  // Other names for the same wires on the sheet: AddrSel = AddrSel_Out

  // Notes on the sheet:
  //   INPUT
  //   OUTPUT
endmodule

module MemRW_processor (
  input  [6:0] Opcode,
  input  [2:0] Funct3,
  input  BrEq,
  input  BrLt,
  output MemRW_Out
);

  wire and_2_out, and_3_out, not_1_out, not_2_out, not_3_out, or_1_out, S;

  and and_1 (S, ~Opcode[2], ~Opcode[3], ~Opcode[4], Opcode[5], ~Opcode[6]);  // AND_Gate
  not not_1 (not_1_out, BrEq);
  not not_2 (not_2_out, Funct3[0]);
  not not_3 (not_3_out, Funct3[2]);
  and and_2 (and_2_out, not_2_out, Funct3[1], not_3_out);
  and and_3 (and_3_out, Funct3[0], Funct3[1], Funct3[2], not_1_out, BrLt);
  or or_1 (or_1_out, and_2_out, and_3_out);
  and and_4 (MemRW_Out, S, or_1_out);

  // Other names for the same wires on the sheet: MemRW = MemRW_Out

  // Notes on the sheet:
  //   INPUT
  //   OUTPUT
endmodule

module WBSel_processor (
  input  [6:0] Opcode,
  input  [2:0] Funct3,
  output [1:0] WBSel_Out
);

  wire I_jalr, IR, not_1_out, not_2_out, not_3_out, not_4_out, not_5_out, not_6_out, not_7_out, not_8_out,
       not_9_out, not_10_out, not_11_out, not_12_out, not_13_out, not_14_out, not_15_out, not_16_out,
       not_17_out, not_18_out, not_19_out, OUT00, OUT01, OUT10, OUT_lui, R, U_auipc, UJ;
  wire [1:0] bitfinder_1_index;

  not not_1 (not_1_out, Opcode[2]);
  not not_2 (not_2_out, Opcode[3]);
  not not_3 (not_3_out, Opcode[6]);
  not not_4 (not_4_out, Opcode[2]);
  not not_5 (not_5_out, Opcode[3]);
  not not_6 (not_6_out, Opcode[5]);
  not not_7 (not_7_out, Opcode[6]);
  not not_8 (not_8_out, Opcode[3]);
  not not_9 (not_9_out, Opcode[6]);
  not not_10 (not_10_out, Opcode[4]);
  not not_11 (not_11_out, Opcode[3]);
  not not_12 (not_12_out, Opcode[4]);
  and and_1 (R, not_1_out, not_2_out, Opcode[4], Opcode[5], not_3_out);
  and and_2 (IR, not_4_out, not_5_out, Opcode[4], not_6_out, not_7_out);
  and and_3 (U_auipc, Opcode[2], not_8_out, Opcode[4], ~Opcode[5], not_9_out);  // AND_Gate
  and and_4 (UJ, Opcode[2], Opcode[3], not_10_out, Opcode[5], Opcode[6]);
  and and_5 (I_jalr, Opcode[2], not_11_out, not_12_out, Opcode[5], Opcode[6]);
  not not_13 (not_13_out, Opcode[2]);
  not not_14 (not_14_out, Opcode[3]);
  not not_15 (not_15_out, Opcode[4]);
  not not_16 (not_16_out, Opcode[5]);
  not not_17 (not_17_out, Opcode[6]);
  not not_18 (not_18_out, Opcode[3]);
  not not_19 (not_19_out, Opcode[6]);
  or or_1 (OUT01, R, U_auipc, IR);
  or or_2 (OUT10, UJ, I_jalr);
  and and_6 (OUT00, not_13_out, not_14_out, not_15_out, not_16_out, not_17_out);
  and and_7 (OUT_lui, Opcode[2], not_18_out, Opcode[4], Opcode[5], not_19_out);
  BitFinder #(.width(4)) bitfinder_1 (.in({OUT_lui, OUT10, OUT01, OUT00}), .index(bitfinder_1_index));  // open: found
  Multiplexer #(.enable("false"), .select(2), .width(2)) multiplexer_1 (
    .in0(2'b00), .in1(2'b01), .in2(2'b10), .in3(2'b11), .out(WBSel_Out), .sel(bitfinder_1_index));

  // Other names for the same wires on the sheet: WBSel[1:0] = WBSel_Out

  // Notes on the sheet:
  //   INPUT
  //   OUTPUT
endmodule

module ALUSel_processor (
  input  [6:0] Opcode,
  input  [2:0] Funct3,
  input  [6:0] Funct7,
  output [3:0] ALUSel_Out
);

  wire and_5_out, and_6_out, and_13_out, and_14_out, and_15_out, and_16_out, and_17_out, and_23_out,
       and_24_out, and_25_out, and_26_out, and_27_out, and_28_out, and_34_out, and_35_out, and_36_out,
       and_37_out, and_38_out, and_39_out, I0000, II0000, IR, IR0000, not_1_out, not_2_out, not_3_out,
       not_4_out, not_5_out, not_6_out, not_7_out, not_8_out, not_9_out, not_10_out, not_11_out, not_12_out,
       not_13_out, not_14_out, not_15_out, not_16_out, not_17_out, not_18_out, not_19_out, not_20_out,
       not_21_out, not_22_out, not_23_out, not_24_out, not_25_out, not_26_out, not_27_out, not_28_out,
       not_29_out, not_30_out, not_31_out, not_32_out, not_33_out, not_34_out, not_35_out, not_36_out,
       not_37_out, not_38_out, not_39_out, not_40_out, not_41_out, not_42_out, not_43_out, not_44_out,
       not_45_out, not_46_out, not_47_out, not_48_out, not_49_out, not_50_out, not_51_out, not_52_out,
       not_53_out, not_54_out, not_55_out, or_2_out, or_3_out, or_4_out, or_5_out, or_6_out, or_7_out,
       OUT0000, OUT0001, OUT0010, OUT0011, OUT0100, OUT0101, OUT0110, OUT0111, OUT1000, OUT1001, OUT1010,
       OUT1011, OUT1100, OUT1110, R, R0000, S0000, SB0000, U0000, UJ0000;
  wire [3:0] bitfinder_1_index;

  not not_1 (not_1_out, Opcode[2]);
  not not_2 (not_2_out, Opcode[3]);
  not not_3 (not_3_out, Opcode[4]);
  not not_4 (not_4_out, Opcode[3]);
  not not_5 (not_5_out, Funct3[0]);
  not not_6 (not_6_out, Funct3[1]);
  not not_7 (not_7_out, Funct3[2]);
  not not_8 (not_8_out, Funct3[0]);
  not not_9 (not_9_out, Funct3[1]);
  not not_10 (not_10_out, Funct3[2]);
  not not_11 (not_11_out, Opcode[4]);
  not not_12 (not_12_out, Opcode[6]);
  not not_13 (not_13_out, Opcode[3]);
  not not_14 (not_14_out, Opcode[4]);
  not not_15 (not_15_out, Funct7[0]);
  not not_16 (not_16_out, Funct7[5]);
  and and_1 (SB0000, not_1_out, not_2_out, not_3_out, Opcode[5], Opcode[6]);
  and and_2 (UJ0000, Opcode[2], Opcode[3], not_11_out, Opcode[5], Opcode[6]);
  and and_3 (U0000, Opcode[2], not_4_out, Opcode[4], not_12_out);
  and and_4 (I0000, Opcode[2], not_13_out, not_14_out, Opcode[5], Opcode[6]);
  and and_5 (and_5_out, not_5_out, not_6_out, not_7_out);
  and and_6 (and_6_out, not_8_out, not_9_out, not_10_out);
  and and_7 (IR0000, IR, and_5_out);
  and and_8 (R0000, R, not_15_out, not_16_out, and_6_out);
  not not_17 (not_17_out, Opcode[2]);
  not not_18 (not_18_out, Opcode[3]);
  not not_19 (not_19_out, Opcode[4]);
  not not_20 (not_20_out, Opcode[5]);
  not not_21 (not_21_out, Opcode[6]);
  not not_22 (not_22_out, Opcode[2]);
  not not_23 (not_23_out, Opcode[3]);
  not not_24 (not_24_out, Opcode[5]);
  not not_25 (not_25_out, Opcode[6]);
  not not_26 (not_26_out, Opcode[2]);
  not not_27 (not_27_out, Opcode[3]);
  not not_28 (not_28_out, Opcode[6]);
  not not_29 (not_29_out, Opcode[2]);
  not not_30 (not_30_out, Opcode[3]);
  not not_31 (not_31_out, Opcode[4]);
  not not_32 (not_32_out, Opcode[6]);
  or or_1 (OUT0000, SB0000, UJ0000, U0000, I0000, IR0000, R0000, S0000, II0000);
  and and_9 (II0000, not_17_out, not_18_out, not_19_out, not_20_out, not_21_out);
  and and_10 (IR, not_22_out, not_23_out, Opcode[4], not_24_out, not_25_out);
  and and_11 (R, not_26_out, not_27_out, Opcode[4], Opcode[5], not_28_out);
  and and_12 (S0000, not_29_out, not_30_out, not_31_out, Opcode[5], not_32_out);
  not not_33 (not_33_out, Funct7[0]);
  not not_34 (not_34_out, Funct3[1]);
  not not_35 (not_35_out, Funct3[2]);
  not not_36 (not_36_out, Funct3[0]);
  not not_37 (not_37_out, Funct3[2]);
  not not_38 (not_38_out, Funct3[0]);
  not not_39 (not_39_out, Funct3[1]);
  not not_40 (not_40_out, Funct3[2]);
  not not_41 (not_41_out, Funct3[0]);
  not not_42 (not_42_out, Funct3[1]);
  not not_43 (not_43_out, Funct3[2]);
  not not_44 (not_44_out, Funct3[0]);
  not not_45 (not_45_out, Funct3[1]);
  or or_2 (or_2_out, IR, R);
  and and_13 (and_13_out, Funct3[0], not_34_out, not_35_out);
  and and_14 (and_14_out, not_38_out, not_39_out, not_40_out);
  and and_15 (and_15_out, not_41_out, not_42_out, not_43_out);
  or or_3 (or_3_out, IR, R);
  and and_16 (and_16_out, not_44_out, not_45_out, Funct3[2]);
  or or_4 (or_4_out, IR, R);
  and and_17 (and_17_out, not_36_out, Funct3[1], not_37_out);
  and and_18 (OUT0011, or_3_out, and_16_out);
  and and_19 (OUT0110, or_2_out, not_33_out, and_13_out);
  and and_20 (OUT0111, or_4_out, and_17_out);
  and and_21 (OUT1100, R, Funct7[5], and_14_out);
  and and_22 (OUT1010, R, Funct7[0], and_15_out);
  not not_46 (not_46_out, Funct3[0]);
  not not_47 (not_47_out, Funct7[5]);
  not not_48 (not_48_out, Funct7[0]);
  not not_49 (not_49_out, Funct3[1]);
  not not_50 (not_50_out, Funct3[1]);
  not not_51 (not_51_out, Funct3[1]);
  not not_52 (not_52_out, Funct3[2]);
  not not_53 (not_53_out, Funct3[1]);
  and and_23 (and_23_out, not_47_out, not_48_out);
  or or_5 (or_5_out, IR, R);
  and and_24 (and_24_out, Funct3[0], not_50_out, Funct3[2]);
  and and_25 (and_25_out, Funct3[0], not_51_out, not_52_out);
  and and_26 (and_26_out, Funct3[0], not_53_out, Funct3[2]);
  or or_6 (or_6_out, IR, R);
  and and_27 (and_27_out, not_46_out, Funct3[1], Funct3[2]);
  or or_7 (or_7_out, IR, R);
  and and_28 (and_28_out, Funct3[0], not_49_out, Funct3[2]);
  and and_29 (OUT0010, or_6_out, and_27_out);
  and and_30 (OUT0100, or_7_out, and_23_out, and_28_out);
  and and_31 (OUT0101, or_5_out, Funct7[5], and_24_out);
  and and_32 (OUT1110, R, Funct7[0], and_25_out);
  and and_33 (OUT1000, R, Funct7[0], and_26_out);
  not not_54 (not_54_out, Funct7[0]);
  not not_55 (not_55_out, Funct3[2]);
  and and_34 (and_34_out, Funct3[0], Funct3[1], Funct3[2]);
  and and_35 (and_35_out, Funct3[0], Funct3[1], Funct3[2]);
  and and_36 (and_36_out, Funct3[0], Funct3[1], not_55_out);
  and and_37 (and_37_out, Funct3[0], Funct3[1], Funct3[2]);
  and and_38 (and_38_out, IR, and_34_out);
  and and_39 (and_39_out, R, not_54_out, and_35_out);
  and and_40 (OUT1011, R, Funct7[0], and_36_out);
  and and_41 (OUT1001, R, Funct7[0], and_37_out);
  or or_8 (OUT0001, and_38_out, and_39_out);
  BitFinder #(.width(14)) bitfinder_1 (
    .in({OUT1110, OUT1100, OUT1011, OUT1010, OUT1001, OUT1000, OUT0111, OUT0110, OUT0101, OUT0100, OUT0011, OUT0010, OUT0001, OUT0000}),
    .index(bitfinder_1_index));  // open: found
  Multiplexer #(.enable("false"), .select(4), .width(4)) multiplexer_1 (
    .in0(4'b0000), .in1(4'b0001), .in2(4'b0010), .in3(4'b0011), .in4(4'b0100), .in5(4'b0101), .in6(4'b0110),
    .in7(4'b0111), .in8(4'b1000), .in9(4'b1001), .in10(4'b1010), .in11(4'b1011), .in12(4'b1100),
    .in13(4'b1110), .out(ALUSel_Out), .sel(bitfinder_1_index));  // open: in14, in15

  // Other names for the same wires on the sheet: ALUSel[3:0] = ALUSel_Out

  // Notes on the sheet:
  //   INPUT
  //   OUTPUT
endmodule
