// Logisim project cpu.circ as structural Verilog: 2 circuits, main circuit main
module main (
  input  [31:0] INSTRUCTION,
  input  CLOCK,
  output [31:0] PROGRAM_COUNTER,
  output [31:0] ra,
  output [31:0] sp,
  output [31:0] t0,
  output [31:0] t1,
  output [31:0] t2,
  output [31:0] s0,
  output [31:0] s1,
  output [31:0] a0
);

  wire AddrSel, ASel, BrEq, BrLt, BrSel, BrUn, BSel, MemRW, PCSel, RegWEn;
  wire [1:0] WBSel;
  wire [2:0] ImmSel;
  wire [3:0] ALUSel;
  wire [31:0] DMEM_output, Imm, Instruction_Q, Instruction_t, multiplexer_1_out, multiplexer_2_out,
       multiplexer_3_out, multiplexer_4_out, multiplexer_5_out, PC_Plus4, PC_Value, PC_Value_Plus4, ReadData,
       Result, rs1, rs2, wb, WriteAddr;

  control_logic control_logic_1 (
    .out_14(AddrSel), .out_4(PCSel), .out_5(RegWEn), .out_6(ImmSel), .out_7(BrUn), .out_8(ASel),
    .out_9(BSel), .out_10(ALUSel), .out_11(MemRW), .out_12(WBSel), .out_13(BrSel), .inst(Instruction_Q),
    .BrEq(BrEq), .BrLt(BrLt));
  Adder #(.width(32)) adder_1 (.a(PROGRAM_COUNTER), .b(32'h4), .out(PC_Plus4));  // open: cin, cout
  Multiplexer #(.enable("false"), .width(32)) multiplexer_1 (
    .in0(PC_Plus4), .in1(Result), .out(multiplexer_1_out), .sel(PCSel));
  imm_gen imm_gen_1 (.imm(Imm), .inst(Instruction_Q), .ImmSel(ImmSel));
  Register #(.width(32)) PC (.D(multiplexer_1_out), .clk(CLOCK), .Q(PROGRAM_COUNTER));  // open: en, clr
  Adder #(.width(32)) adder_2 (.a(PC_Value), .b(32'h4), .out(PC_Value_Plus4));  // open: cin, cout
  Register #(.width(32)) register_1 (.D(PROGRAM_COUNTER), .clk(CLOCK), .Q(PC_Value));  // open: en, clr
  Multiplexer #(.enable("false"), .width(32)) multiplexer_2 (
    .in0(rs2), .in1(Imm), .out(multiplexer_2_out), .sel(BrSel));
  branch_comp branch_comp_1 (.BrEq(BrEq), .BrLt(BrLt), .rs1(rs1), .rs2(multiplexer_2_out), .BrUn(BrUn));
  Multiplexer #(.enable("false"), .width(32)) multiplexer_3 (
    .in0(Instruction_t), .in1(32'h13), .out(multiplexer_3_out), .sel(PCSel));
  Register #(.width(32)) register_2 (.D(multiplexer_3_out), .clk(CLOCK), .Q(Instruction_Q));  // open: en, clr
  Multiplexer #(.enable("false"), .width(32)) multiplexer_4 (.in0(rs2), .in1(Imm), .out(multiplexer_4_out), .sel(BSel));
  Multiplexer #(.enable("false"), .width(32)) multiplexer_5 (
    .in0(rs1), .in1(PC_Value), .out(multiplexer_5_out), .sel(ASel));
  alu Arithmetic_Logic_Unit (.Result(Result), .A(multiplexer_5_out), .B(multiplexer_4_out), .ALUSel(ALUSel));
  Multiplexer #(.enable("false"), .width(32)) multiplexer_6 (.in0(Result), .in1(rs1), .out(WriteAddr), .sel(AddrSel));
  // mem_main DMEM: pin names not known; wires that end beside it: WriteAddr, rs2, CLOCK, MemRW, DMEM_output
  Multiplexer #(.enable("false"), .select(2), .width(32)) multiplexer_7 (
    .in0(ReadData), .in1(Result), .in2(PC_Value_Plus4), .in3(Imm), .out(wb), .sel(WBSel));
  regfile_main RegFile (
    .s1(s1), .a0(a0), .Read_Data_1(rs1), .Read_Data_2(rs2), .ra(ra), .sp(sp), .t0(t0), .t1(t1), .t2(t2),
    .s0(s0), .RegWEn(RegWEn), .clk(CLOCK), .Write_Data(wb), .rs1(Instruction_Q[19:15]),
    .rs2(Instruction_Q[24:20]), .rd(Instruction_Q[11:7]));
  after_DMEM after_dmem_1 (
    .Addr(Result), .funct3(Instruction_Q[14:12]), .DMEM_output(DMEM_output), .real_output(ReadData));

  // Other names for the same wires on the sheet: clk = CLOCK

  // Notes on the sheet:
  //   Output
  //   IMEM (do **NOT** move this)
  //   Inputs
  //   Inputs/Outputs for testing. Do **NOT** move these.
endmodule

module after_DMEM (
  input  [31:0] Addr,
  input  [2:0] funct3,
  input  [31:0] DMEM_output,
  output [31:0] real_output
);

  wire [31:0] lb, lh;

  Multiplexer #(.enable("false"), .select(2), .width(32)) multiplexer_1 (
    .in0({{25{DMEM_output[7]}}, DMEM_output[6:0]}), .in1({{25{DMEM_output[15]}}, DMEM_output[14:8]}),
    .in2({{25{DMEM_output[23]}}, DMEM_output[22:16]}), .in3({{25{DMEM_output[31]}}, DMEM_output[30:24]}),
    .out(lb), .sel(Addr[1:0]));
  Multiplexer #(.enable("false"), .width(32)) multiplexer_2 (
    .in0({{17{DMEM_output[15]}}, DMEM_output[14:0]}), .in1({{17{DMEM_output[31]}}, DMEM_output[30:16]}),
    .out(lh), .sel(Addr[1]));
  Multiplexer #(.enable("false"), .select(3), .width(32)) multiplexer_3 (
    .in0(lb), .in1(lh), .in2(DMEM_output), .out(real_output), .sel(funct3));  // open: in3, in4, in5, in6, in7

  // Other names for the same wires on the sheet: byte0[31:0] = {{25{DMEM_output[7]}}, DMEM_output[6:0]};
  //   half0[31:0] = {{17{DMEM_output[15]}}, DMEM_output[14:0]}; lw[31:0] = DMEM_output;
  //   byte1[31:0] = {{25{DMEM_output[15]}}, DMEM_output[14:8]};
  //   byte2[31:0] = {{25{DMEM_output[23]}}, DMEM_output[22:16]};
  //   half1[31:0] = {{17{DMEM_output[31]}}, DMEM_output[30:16]};
  //   byte3[31:0] = {{25{DMEM_output[31]}}, DMEM_output[30:24]}
endmodule
