// Logisim project cpu_original.circ as structural Verilog: 1 circuit, main circuit main
module main (
  input  [31:0] INSTRUCTION,
  input  CLOCK,
  output [31:0] PROGRAM_COUNTER,
  output [31:0] ra,
  output [31:0] sp,
  output [31:0] t0,
  output [31:0] t1,
  output [31:0] t2,
  output [31:0] s0,
  output [31:0] s1,
  output [31:0] a0
);

  wire [2:0] ImmSel;
  wire [3:0] ALUSel;
  wire [31:0] adder_1_out, Imm, multiplexer_1_out, rs1, rs2, wb;

  // control_logic control_logic_1: pin names not known
  Adder #(.width(32)) adder_1 (.a(PROGRAM_COUNTER), .b(32'h4), .out(adder_1_out));  // open: cin, cout
  Register #(.width(32)) PC (.D(adder_1_out), .clk(CLOCK), .Q(PROGRAM_COUNTER));  // open: en, clr
  imm_gen imm_gen_1 (.imm(Imm), .inst(INSTRUCTION), .ImmSel(ImmSel));
  // branch_comp branch_comp_1: pin names not known
  regfile_main RegFile (
    .s1(s1), .a0(a0), .ra(ra), .sp(sp), .t0(t0), .t1(t1), .t2(t2), .s0(s0), .Write_Data(wb),
    .rs1(INSTRUCTION[19:15]), .rs2(INSTRUCTION[24:20]), .rd(INSTRUCTION[11:7]));  // open: Read_Data_1, Read_Data_2, RegWEn, clk
  Multiplexer #(.enable("false"), .width(32)) multiplexer_1 (.in0(rs2), .in1(Imm), .out(multiplexer_1_out), .sel(1'b1));
  alu Arithmetic_Logic_Unit (.Result(wb), .A(rs1), .B(multiplexer_1_out), .ALUSel(ALUSel));
  // mem_main DMEM: pin names not known

  // Other names for the same wires on the sheet: clk = CLOCK

  // Notes on the sheet:
  //   Output
  //   IMEM (do **NOT** move this)
  //   Inputs
  //   Inputs/Outputs for testing. Do **NOT** move these.
endmodule
