// Logisim project imm_gen.circ as structural Verilog: 1 circuit, main circuit imm_gen
module imm_gen (
  input  [31:0] inst,
  input  [2:0] ImmSel,
  output [31:0] imm
);


  // Other names for the same wires on the sheet: imm_IFormat[31:0] = {{21{inst[31]}}, inst[30:20]};
  //   imm_IR[31:0] = {{28{inst[24]}}, inst[23:20]}; imm_UFormat[31:12] = inst[31:12]; imm_UJFormat[31:1] = inst[31:1];
  //   imm_SBFormat[31:1] = {{20{inst[31]}}, inst[7], inst[30:25], inst[11:8]};
  //   imm_SFormat[31:0] = {{21{inst[31]}}, inst[30:25], inst[11:7]}

  // Notes on the sheet:
  //   INPUTS to your circuit
  //   DON'T CHANGE THE LOCATIONS OF THE INPUTS AND OUTPUTS!
  //   OUTPUT from your circuit
endmodule
